# Fritzing sketch Subarino (saved by Fritzing 0.9.3b)

parts:
  Часть1 = Arduino Uno (Rev3)
  Часть2 = Bluetooth HC-05 Macho
  Часть3 = BH1750
  Часть4 = Relay
  Часть5 = Relay

nets:
  N1: Часть1.A3, Часть3.ADDR
  N2: Часть1.A4/SDA, Часть3.SDA
  N3: Часть1.A5/SCL, Часть3.SCL
  N4: Часть1.D8, Часть4.SIGNAL
  N5: Часть1.D9_PWM, Часть5.SIGNAL
  N6: Часть1.D2, Часть2.RXD
  N7: Часть1.D3_PWM, Часть2.TXD
  3V3: Часть1.3V3, Часть3.VCC
  VCC: Часть1.5V, Часть2.VCC, Часть4.VCC, Часть5.VCC
  GND: Часть1.GND, Часть2.GND, Часть3.GND, Часть4.GND, Часть5.GND

custom parts:
  BH1750: Light Sensor
  Relay: The official support forum: support@iteadstudio.com
